// Logisim project s-mips-template.circ as structural Verilog: 11 circuits, main circuit S-MIPS Board
module S_MIPS_Board (
  input  DESHABILITAR_DISPATCHER,
  output halt
);

  wire button_1_out, CLK, CS, d_ff_1_q, LCLR, LoadRAM, LoadRAMOn, LW, R_R_W, R_W, ram_dispatcher_1_finished,
       RCS, Reset_out, RST, TTY_EN;
  wire [2:0] KDB;
  wire [3:0] LMask, Mask, ram_1_read_time, ram_1_write_time, RMask;
  wire [6:0] KDB_DATA, TTY_DATA;
  wire [15:0] Addr, LAddr, RAddr;
  wire [31:0] I0, I1, I2, I3, LData, ram_1_data_out_0, ram_1_data_out_1, ram_1_data_out_2, ram_1_data_out_3,
       RI0, RI1, RI2, RI3;

  TTY #(.rows(25), .cols(80)) tty_1 (.data(TTY_DATA), .clk(CLK), .we(TTY_EN), .clr(RST));
  not not_1 (LoadRAMOn, ram_dispatcher_1_finished);
  RAM_Dispatcher ram_dispatcher_1 (
    .WriteTime(ram_1_write_time), .Clock(CLK), .Data(LData), .Address(LAddr), .Mask(LMask),
    .Finished(ram_dispatcher_1_finished), .Write(LW), .CLR(LCLR));
  Keyboard #(.buflen(64)) keyboard_1 (.clk(CLK), .re(KDB[0]), .avail(KDB[2]), .data(KDB_DATA));  // open: clr
  RAM ram_1 (
    .Address(RAddr), .Data_Out_0(ram_1_data_out_0), .Data_Out_1(ram_1_data_out_1),
    .Data_Out_2(ram_1_data_out_2), .Data_Out_3(ram_1_data_out_3), .Data_In_0(RI0), .Data_In_1(RI1),
    .Data_In_2(RI2), .Data_In_3(RI3), .Mask(RMask), .nRead_Write(R_R_W), .Chip_Select(RCS),
    .Read_Time(ram_1_read_time), .Reset(button_1_out), .Write_Time(ram_1_write_time));
  Button button_1 (.out(button_1_out));
  D_Flip_Flop d_ff_1 (.clk(CLK), .D(1'b1), .Q(d_ff_1_q), .reset(Reset_out));  // open: Qn, preset, en
  Button Reset (.out(Reset_out));
  S_MIPS s_mips_1 (
    .Kbd_Enable(KDB[0]), .Address(Addr), .Kbd_Clear(KDB[1]), .Kbd_Available(KDB[2]), .RAM_In_0(I0),
    .Kbd_ASCII_Data(KDB_DATA), .RAM_In_1(I1), .TTY_Enable(TTY_EN), .RAM_In_2(I2), .RAM_In_3(I3),
    .TTY_ASCII_Data(TTY_DATA), .Reset(RST), .RAM_Out_0(ram_1_data_out_0), .Clock(CLK),
    .RAM_Out_1(ram_1_data_out_1), .Stop(halt), .RAM_Out_2(ram_1_data_out_2), .RAM_Out_3(ram_1_data_out_3),
    .Mask(Mask), .Read_Time(ram_1_read_time), .Write_Time(ram_1_write_time), .nRead_Write(R_W),
    .Chip_Select(CS));
  D_Flip_Flop d_ff_2 (.clk(CLK), .D(d_ff_1_q), .Qn(LCLR), .reset(Reset_out));  // open: Q, preset, en
  or or_1 (RST, LCLR, LoadRAM);
  Clock clock_1 (.out(CLK));
  Multiplexer #(.width(32), .enable("false")) multiplexer_1 (.in0(I0), .in1(LData), .out(RI0), .sel(LoadRAM));
  Multiplexer #(.width(32), .enable("false")) multiplexer_2 (.in0(I1), .in1(LData), .out(RI1), .sel(LoadRAM));
  Multiplexer #(.width(32), .enable("false")) multiplexer_3 (.in0(I2), .in1(LData), .out(RI2), .sel(LoadRAM));
  Multiplexer #(.width(32), .enable("false")) multiplexer_4 (.in0(I3), .in1(LData), .out(RI3), .sel(LoadRAM));
  and and_1 (LoadRAM, ~DESHABILITAR_DISPATCHER, LoadRAMOn);  // AND_Gate
  Multiplexer #(.width(16), .enable("false")) multiplexer_5 (.in0(Addr), .in1(LAddr), .out(RAddr), .sel(LoadRAM));
  Multiplexer #(.width(4), .enable("false")) multiplexer_6 (.in0(Mask), .in1(LMask), .out(RMask), .sel(LoadRAM));
  Multiplexer #(.enable("false")) multiplexer_7 (.in0(CS), .in1(LW), .out(RCS), .sel(LoadRAM));
  Multiplexer #(.enable("false")) multiplexer_8 (.in0(R_W), .in1(LW), .out(R_R_W), .sel(LoadRAM));

  // Notes on the sheet:
  //   NO MODIFICAR
  //   Keyboard
endmodule

module RAM (
  input  [15:0] Address,
  input  [31:0] Data_In_0,
  input  [31:0] Data_In_1,
  input  [31:0] Data_In_2,
  input  [31:0] Data_In_3,
  input  [3:0] Mask,
  input  nRead_Write,
  input  Chip_Select,
  input  Reset,
  output [31:0] Data_Out_0,
  output [31:0] Data_Out_1,
  output [31:0] Data_Out_2,
  output [31:0] Data_Out_3,
  output [3:0] Read_Time,
  output [3:0] Write_Time
);

  wire and_2_out, and_3_out, and_4_out, and_5_out, and_6_out, and_7_out, and_8_out, and_9_out, Changed, CLK,
       comparator_2_eq, comparator_3_eq, comparator_4_eq, comparator_5_eq, comparator_6_eq, Count,
       demultiplexer_3_out0, Idle, Idle_q, Load, Load0, Load1, nand_1_out, or_1_out, or_2_out, or_3_out,
       or_4_out, or_5_out, or_6_out, or_7_out, or_8_out, or_9_out, or_10_out, Proc_q, Update_Mem, Zero_Time;
  wire [3:0] counter_1_q, multiplexer_1_out, subtractor_1_out;
  wire [31:0] register_1_q, register_2_q, register_3_q, register_4_q, register_5_q;

  // Probe on 4'b0011
  // Probe on 4'b0010
  Multiplexer #(.width(4), .enable("false")) multiplexer_1 (
    .in0(4'b0011), .in1(4'b0010), .out(multiplexer_1_out), .sel(nRead_Write));
  or or_1 (or_1_out, Idle, Update_Mem);
  or or_2 (or_2_out, ~Chip_Select, Reset);  // OR_Gate
  Subtractor #(.width(4)) subtractor_1 (.a(multiplexer_1_out), .b(4'b0010), .out(subtractor_1_out));  // open: bin, bout
  Demultiplexer #(.enable("false")) demultiplexer_1 (.out0(Idle), .out1(Load0), .in(Idle_q), .sel(Changed));
  D_Flip_Flop u_Idle (.clk(CLK), .D(or_1_out), .Q(Idle_q), .preset(or_2_out));  // open: Qn, en, reset
  // Probe on counter_1_q
  Counter #(.width(4), .max('hf)) counter_1 (
    .load(Load), .D(subtractor_1_out), .count(Count), .Q(counter_1_q), .clk(CLK), .clr(or_3_out));  // open: carry
  or or_3 (or_3_out, ~Chip_Select, Reset);  // OR_Gate
  Comparator #(.width(4), .mode("unsigned")) comparator_1 (
    .a(4'b0000), .b(counter_1_q), .eq(Zero_Time));  // open: gt, lt
  or or_4 (or_4_out, Count, Load0, Load1);
  Register #(.width(32)) register_1 (.D(Data_In_0), .en(Chip_Select), .Q(register_1_q), .clk(CLK), .clr(or_5_out));
  or or_5 (or_5_out, ~Chip_Select, Reset);  // OR_Gate
  Register #(.width(32)) register_2 (.D(Data_In_1), .en(Chip_Select), .Q(register_2_q), .clk(CLK), .clr(or_6_out));
  or or_6 (or_6_out, ~Chip_Select, Reset);  // OR_Gate
  Register #(.width(32)) register_3 (.D(Data_In_2), .en(Chip_Select), .Q(register_3_q), .clk(CLK), .clr(or_7_out));
  or or_7 (or_7_out, ~Chip_Select, Reset);  // OR_Gate
  Register #(.width(32)) register_4 (.D(Data_In_3), .en(Chip_Select), .Q(register_4_q), .clk(CLK), .clr(or_8_out));
  or or_8 (or_8_out, ~Chip_Select, Reset);  // OR_Gate
  Register #(.width(32)) register_5 (
    .D({{11{1'b1}}, nRead_Write, Mask, Address}), .en(Chip_Select), .Q(register_5_q), .clk(CLK),
    .clr(or_9_out));
  or or_9 (or_9_out, ~Chip_Select, Reset);  // OR_Gate
  D_Flip_Flop Proc (.clk(CLK), .D(or_4_out), .Q(Proc_q), .reset(or_10_out));  // open: Qn, preset, en
  or or_10 (or_10_out, ~Chip_Select, Reset);  // OR_Gate
  Demultiplexer #(.enable("false")) demultiplexer_2 (
    .out0(Count), .out1(Update_Mem), .in(demultiplexer_3_out0), .sel(Zero_Time));
  Demultiplexer #(.enable("false")) demultiplexer_3 (
    .out0(demultiplexer_3_out0), .out1(Load1), .in(Proc_q), .sel(Changed));
  Clock clock_1 (.out(CLK));
  Comparator #(.width(32)) comparator_2 (.a(register_1_q), .b(Data_In_0), .eq(comparator_2_eq));  // open: gt, lt
  Comparator #(.width(32)) comparator_3 (.a(register_2_q), .b(Data_In_1), .eq(comparator_3_eq));  // open: gt, lt
  Comparator #(.width(32)) comparator_4 (.a(register_3_q), .b(Data_In_2), .eq(comparator_4_eq));  // open: gt, lt
  Comparator #(.width(32)) comparator_5 (.a(register_4_q), .b(Data_In_3), .eq(comparator_5_eq));  // open: gt, lt
  Comparator #(.width(32)) comparator_6 (
    .a(register_5_q), .b({{11{1'b1}}, nRead_Write, Mask, Address}), .eq(comparator_6_eq));  // open: gt, lt
  nand nand_1 (nand_1_out, comparator_6_eq, comparator_2_eq, comparator_3_eq, comparator_4_eq, comparator_5_eq);
  and and_1 (Changed, nand_1_out, Chip_Select);
  or or_11 (Load, Count, Load1, Load0);
  and and_2 (and_2_out, Mask[0], Update_Mem, nRead_Write);
  and and_3 (and_3_out, Mask[1], Update_Mem, nRead_Write);
  and and_4 (and_4_out, Mask[2], Update_Mem, nRead_Write);
  and and_5 (and_5_out, Mask[3], Update_Mem, nRead_Write);
  RAM_part #(.addrWidth(16), .dataWidth(32), .bus("separate")) ram_1 (
    .addr(Address), .din(Data_In_0), .data(Data_Out_0), .str(and_2_out), .sel(Chip_Select), .clk(CLK),
    .ld(and_6_out), .clr(Reset));
  and and_6 (and_6_out, ~nRead_Write, Idle);  // AND_Gate
  RAM_part #(.addrWidth(16), .dataWidth(32), .bus("separate")) ram_2 (
    .addr(Address), .din(Data_In_1), .data(Data_Out_1), .str(and_3_out), .sel(Chip_Select), .clk(CLK),
    .ld(and_7_out), .clr(Reset));
  and and_7 (and_7_out, ~nRead_Write, Idle);  // AND_Gate
  RAM_part #(.addrWidth(16), .dataWidth(32), .bus("separate")) ram_3 (
    .addr(Address), .din(Data_In_2), .data(Data_Out_2), .str(and_4_out), .sel(Chip_Select), .clk(CLK),
    .ld(and_8_out), .clr(Reset));
  and and_8 (and_8_out, ~nRead_Write, Idle);  // AND_Gate
  RAM_part #(.addrWidth(16), .dataWidth(32), .bus("separate")) ram_4 (
    .addr(Address), .din(Data_In_3), .data(Data_Out_3), .str(and_5_out), .sel(Chip_Select), .clk(CLK),
    .ld(and_9_out), .clr(Reset));
  and and_9 (and_9_out, ~nRead_Write, Idle);  // AND_Gate

  assign Read_Time = 4'b0011;
  assign Write_Time = 4'b0010;

  // Other names for the same wires on the sheet: M0 = Mask[0]; M1 = Mask[1]; M2 = Mask[2]; M3 = Mask[3];
  //   RW = nRead_Write; CLR = Reset; CS = Chip_Select; Load2 = Count

  // Notes on the sheet:
  //   NO MODIFICAR
  //   excepto quizás los valores RT y WT
  //   BANK0
  //   BANK1
  //   BANK2
  //   BANK3
endmodule

module S_MIPS (
  input  Kbd_Available,
  input  [6:0] Kbd_ASCII_Data,
  input  [31:0] RAM_Out_0,
  input  [31:0] RAM_Out_1,
  input  Reset,
  input  [31:0] RAM_Out_2,
  input  Clock,
  input  [31:0] RAM_Out_3,
  input  [3:0] Read_Time,
  input  [3:0] Write_Time,
  output Kbd_Enable,
  output [15:0] Address,
  output Kbd_Clear,
  output TTY_Enable,
  output [6:0] TTY_ASCII_Data,
  output Stop,
  output [31:0] RAM_In_0,
  output [31:0] RAM_In_1,
  output [31:0] RAM_In_2,
  output [31:0] RAM_In_3,
  output [3:0] Mask,
  output nRead_Write,
  output Chip_Select
);


  // Other names for the same wires on the sheet: CLK = Clock; CLR = Reset; CS = Chip_Select;
  //   KBD_AVAIL = Kbd_Available; KBD_CLR = Kbd_Clear; KBD_DATA[6:0] = Kbd_ASCII_Data; RAM_A[15:0] = Address;
  //   RAM_INPUT_0[31:0] = RAM_In_0; RAM_INPUT_1[31:0] = RAM_In_1; RAM_INPUT_2[31:0] = RAM_In_2;
  //   RAM_INPUT_3[31:0] = RAM_In_3; RAM_MASK[3:0] = Mask; RAM_OUTPUT_0[31:0] = RAM_Out_0;
  //   RAM_OUTPUT_1[31:0] = RAM_Out_1; RAM_OUTPUT_2[31:0] = RAM_Out_2; RAM_OUTPUT_3[31:0] = RAM_Out_3;
  //   RW = nRead_Write; TTY_DATA[6:0] = TTY_ASCII_Data

  // Notes on the sheet:
  //   RAM ADDRESS
  //   DATA FROM RAM
  //   DATA TO RAM
  //   DATA WRITE MASK
  //   RAM TIMING
  //   RAM CONTROL
  //   KEYBOARD
  //   TTY
  //   SEQUENCING
endmodule

module RAM_Dispatcher (
  input  [3:0] WriteTime,
  input  Clock,
  input  CLR,
  output [31:0] Data,
  output [15:0] Address,
  output [3:0] Mask,
  output Finished,
  output Write
);

  wire demultiplexer_2_out1, demultiplexer_3_out1, End, IDLE_q, IncAddr, Load, or_1_out, or_2_out, While_q,
       WriteEnd;
  wire [3:0] counter_1_q;
  wire [31:0] CurrentAddress_q;

  Counter #(.width(32), .max('hffffffff)) CurrentAddress (
    .count(IncAddr), .Q({CurrentAddress_q[31:18], Address, CurrentAddress_q[1:0]}), .clk(Clock), .clr(CLR));  // open: load, D, carry
  or or_1 (or_1_out, IncAddr, demultiplexer_3_out1, Finished);
  D_Flip_Flop IDLE (.clk(Clock), .D(or_1_out), .Q(IDLE_q), .preset(CLR));  // open: Qn, en, reset
  Demultiplexer #(.enable("false")) demultiplexer_1 (.out0(Load), .out1(Finished), .in(IDLE_q), .sel(End));
  D_Flip_Flop While (.clk(Clock), .D(or_2_out), .Q(While_q), .reset(CLR));  // open: Qn, preset, en
  or or_2 (or_2_out, Write, Load);
  RAM_part #(.addrWidth(18), .dataWidth(32)) ram_1 (
    .addr({Address, CurrentAddress_q[1:0]}), .data(Data), .clk(Clock));  // open: sel, ld, clr
  Demultiplexer #(.enable("false")) demultiplexer_2 (
    .out0(Write), .out1(demultiplexer_2_out1), .in(While_q), .sel(WriteEnd));
  Decoder #(.select(2)) decoder_1 (
    .out0(Mask[0]), .out1(Mask[1]), .out2(Mask[2]), .out3(Mask[3]), .sel(CurrentAddress_q[1:0]));  // open: en
  Demultiplexer #(.enable("false")) demultiplexer_3 (
    .out0(IncAddr), .out1(demultiplexer_3_out1), .in(demultiplexer_2_out1), .sel(End));
  Counter #(.width(4), .max('hf)) counter_1 (
    .load(Load), .D(WriteTime), .count(Write), .Q(counter_1_q), .clk(Clock));  // open: carry, clr
  Comparator #(.width(32)) comparator_1 (.a(Data), .b({32{1'b1}}), .eq(End));  // open: gt, lt
  Comparator #(.width(4)) comparator_2 (.a(4'b0000), .b(counter_1_q), .eq(WriteEnd));  // open: gt, lt

  // Other names for the same wires on the sheet: CLK = Clock; Count = Write; WT[3:0] = WriteTime
endmodule

module ALU (
  input  [31:0] A,
  input  [31:0] B,
  input  [3:0] Op,
  output [31:0] R
);

  wire [31:0] adder_1_out, and_1_out, divider_1_out, multiplier_1_out, nor_1_out, or_1_out,
       sign_divider_1_out_3, sign_multiplier_1_out_3, slt_1_out_3, slt_unsign_1_out_3, subtractor_1_out,
       xor_1_out;

  Adder #(.width(32)) adder_1 (.a(A), .b(B), .out(adder_1_out), .cin(1'b0));  // open: cout
  Subtractor #(.width(32)) subtractor_1 (.a(A), .b(B), .out(subtractor_1_out), .bin(1'b0));  // open: bout
  Multiplier #(.width(32)) multiplier_1 (.a(A), .b(B), .out(multiplier_1_out));  // open: cin, cout
  Divider #(.width(32)) divider_1 (.a(A), .b(B), .out(divider_1_out));  // open: upper, rem
  assign and_1_out = A & B;  // AND_Gate and_1, 32 bits wide
  assign or_1_out = A | B;  // OR_Gate or_1, 32 bits wide
  assign xor_1_out = A ^ B;  // XOR_Gate xor_1, 32 bits wide
  assign nor_1_out = ~(A | B);  // NOR_Gate nor_1, 32 bits wide
  Sign_Multiplier sign_multiplier_1 (.A(A), .B(B), .out_3(sign_multiplier_1_out_3));
  Sign_Divider sign_divider_1 (.A(A), .B(B), .out_3(sign_divider_1_out_3));
  slt slt_1 (.A(A), .B(B), .out_3(slt_1_out_3));
  slt_unsign slt_unsign_1 (.A(A), .B(B), .out_3(slt_unsign_1_out_3));
  Multiplexer #(.select(4), .width(32), .enable("false")) multiplexer_1 (
    .in0(adder_1_out), .in1(subtractor_1_out), .in2(multiplier_1_out), .in3(divider_1_out), .in4(and_1_out),
    .in5(or_1_out), .in6(xor_1_out), .in7(nor_1_out), .in8(sign_multiplier_1_out_3),
    .in9(sign_divider_1_out_3), .in10(slt_1_out_3), .in11(slt_unsign_1_out_3), .out(R), .sel(Op));  // open: in12, in13, in14, in15
endmodule

module Sign_Multiplier (
  input  [31:0] A,
  input  [31:0] B,
  output [31:0] out_3
);

  wire comparator_1_eq, comparator_2_eq, comparator_3_eq, not_4_out;
  wire [31:0] adder_1_out, adder_2_out, adder_3_out, multiplexer_1_out, multiplexer_2_out, multiplier_1_out,
       not_1_out, not_2_out, not_3_out;

  Comparator #(.width(1)) comparator_1 (.a(A[31]), .b(1'b1), .eq(comparator_1_eq));  // open: gt, lt
  Comparator #(.width(1)) comparator_2 (.a(B[31]), .b(1'b1), .eq(comparator_2_eq));  // open: gt, lt
  assign not_1_out = ~A;  // NOT_Gate not_1, 32 bits wide
  assign not_2_out = ~B;  // NOT_Gate not_2, 32 bits wide
  Adder #(.width(32)) adder_1 (.a(not_2_out), .b(32'h1), .out(adder_1_out));  // open: cin, cout
  Adder #(.width(32)) adder_2 (.a(not_1_out), .b(32'h1), .out(adder_2_out));  // open: cin, cout
  Multiplexer #(.width(32), .enable("false")) multiplexer_1 (
    .in0(A), .in1(adder_2_out), .out(multiplexer_1_out), .sel(comparator_1_eq));
  Multiplexer #(.width(32), .enable("false")) multiplexer_2 (
    .in0(B), .in1(adder_1_out), .out(multiplexer_2_out), .sel(comparator_2_eq));
  Multiplier #(.width(32)) multiplier_1 (
    .a(multiplexer_1_out), .b(multiplexer_2_out), .out(multiplier_1_out));  // open: cin, cout
  Comparator #(.width(1)) comparator_3 (
    .a(comparator_1_eq), .b(comparator_2_eq), .eq(comparator_3_eq));  // open: gt, lt
  assign not_3_out = ~multiplier_1_out;  // NOT_Gate not_3, 32 bits wide
  Adder #(.width(32)) adder_3 (.a(not_3_out), .b(32'h1), .out(adder_3_out));  // open: cin, cout
  not not_4 (not_4_out, comparator_3_eq);
  Multiplexer #(.width(32), .enable("false")) multiplexer_3 (
    .in0(multiplier_1_out), .in1(adder_3_out), .out(out_3), .sel(not_4_out));
endmodule

module Sign_Divider (
  input  [31:0] A,
  input  [31:0] B,
  output [31:0] out_3
);

  wire comparator_1_eq, comparator_2_eq, comparator_3_eq, not_4_out;
  wire [31:0] adder_1_out, adder_2_out, adder_3_out, divider_1_out, multiplexer_1_out, multiplexer_2_out,
       not_1_out, not_2_out, not_3_out;

  Comparator #(.width(1)) comparator_1 (.a(A[31]), .b(1'b1), .eq(comparator_1_eq));  // open: gt, lt
  Comparator #(.width(1)) comparator_2 (.a(B[31]), .b(1'b1), .eq(comparator_2_eq));  // open: gt, lt
  assign not_1_out = ~A;  // NOT_Gate not_1, 32 bits wide
  assign not_2_out = ~B;  // NOT_Gate not_2, 32 bits wide
  Adder #(.width(32)) adder_1 (.a(not_2_out), .b(32'h1), .out(adder_1_out));  // open: cin, cout
  Adder #(.width(32)) adder_2 (.a(not_1_out), .b(32'h1), .out(adder_2_out));  // open: cin, cout
  Multiplexer #(.width(32), .enable("false")) multiplexer_1 (
    .in0(A), .in1(adder_2_out), .out(multiplexer_1_out), .sel(comparator_1_eq));
  Multiplexer #(.width(32), .enable("false")) multiplexer_2 (
    .in0(B), .in1(adder_1_out), .out(multiplexer_2_out), .sel(comparator_2_eq));
  Divider #(.width(32)) divider_1 (
    .a(multiplexer_1_out), .b(multiplexer_2_out), .out(divider_1_out));  // open: upper, rem
  Comparator #(.width(1)) comparator_3 (
    .a(comparator_1_eq), .b(comparator_2_eq), .eq(comparator_3_eq));  // open: gt, lt
  assign not_3_out = ~divider_1_out;  // NOT_Gate not_3, 32 bits wide
  Adder #(.width(32)) adder_3 (.a(not_3_out), .b(32'h1), .out(adder_3_out));  // open: cin, cout
  not not_4 (not_4_out, comparator_3_eq);
  Multiplexer #(.width(32), .enable("false")) multiplexer_3 (
    .in0(divider_1_out), .in1(adder_3_out), .out(out_3), .sel(not_4_out));
endmodule

module slt (
  input  [31:0] A,
  input  [31:0] B,
  output [31:0] out_3
);

  Comparator #(.width(32)) comparator_1 (.a(A), .b(B), .lt(out_3[0]));  // open: gt, eq

  assign out_3[31:1] = {31{1'b0}};
endmodule

module slt_unsign (
  input  [31:0] A,
  input  [31:0] B,
  output [31:0] out_3
);

  Comparator #(.width(32), .mode("unsigned")) comparator_1 (.a(A), .b(B), .lt(out_3[0]));  // open: gt, eq

  assign out_3[31:1] = {31{1'b0}};
endmodule

// W
module RF (
  input  RW,
  input  [31:0] DI,
  input  [4:0] DA,
  input  Rst,
  input  [4:0] Sa,
  input  [4:0] Sb,
  output [31:0] A,
  output [31:0] B
);

  wire and_1_out, and_2_out, and_3_out, and_4_out, and_5_out, and_6_out, and_7_out, and_8_out, and_9_out,
       and_10_out, and_11_out, and_12_out, and_13_out, and_14_out, and_15_out, and_16_out, and_17_out,
       and_18_out, and_19_out, and_20_out, and_21_out, and_22_out, and_23_out, and_24_out, and_25_out,
       and_26_out, and_27_out, and_28_out, and_29_out, and_30_out, and_31_out, and_32_out, clk,
       decoder_1_out0, decoder_1_out1, decoder_1_out2, decoder_1_out3, decoder_1_out4, decoder_1_out5,
       decoder_1_out6, decoder_1_out7, decoder_1_out8, decoder_1_out9, decoder_1_out10, decoder_1_out11,
       decoder_1_out12, decoder_1_out13, decoder_1_out14, decoder_1_out15, decoder_1_out16, decoder_1_out17,
       decoder_1_out18, decoder_1_out19, decoder_1_out20, decoder_1_out21, decoder_1_out22, decoder_1_out23,
       decoder_1_out24, decoder_1_out25, decoder_1_out26, decoder_1_out27, decoder_1_out28, decoder_1_out29,
       decoder_1_out30, decoder_1_out31;
  wire [31:0] R0, R1, R2, R3, R4, R5, R6, R7, R8, R9, R10, R11, R12, R13, R14, R15, R16, R17, R18, R19, R20,
       R21, R22, R23, R24, R25, R26, R27, R28, R29, R30, R31;

  Clock clock_1 (.out(clk));
  Decoder #(.select(5)) decoder_1 (
    .out0(decoder_1_out0), .out1(decoder_1_out1), .out2(decoder_1_out2), .out3(decoder_1_out3),
    .out4(decoder_1_out4), .out5(decoder_1_out5), .out6(decoder_1_out6), .out7(decoder_1_out7),
    .out8(decoder_1_out8), .out9(decoder_1_out9), .out10(decoder_1_out10), .out11(decoder_1_out11),
    .out12(decoder_1_out12), .out13(decoder_1_out13), .out14(decoder_1_out14), .out15(decoder_1_out15),
    .out16(decoder_1_out16), .out17(decoder_1_out17), .out18(decoder_1_out18), .out19(decoder_1_out19),
    .out20(decoder_1_out20), .out21(decoder_1_out21), .out22(decoder_1_out22), .out23(decoder_1_out23),
    .out24(decoder_1_out24), .out25(decoder_1_out25), .out26(decoder_1_out26), .out27(decoder_1_out27),
    .out28(decoder_1_out28), .out29(decoder_1_out29), .out30(decoder_1_out30), .out31(decoder_1_out31),
    .sel(DA));  // open: en
  and and_1 (and_1_out, RW, decoder_1_out0);
  and and_2 (and_2_out, RW, decoder_1_out1);
  and and_3 (and_3_out, RW, decoder_1_out2);
  and and_4 (and_4_out, RW, decoder_1_out3);
  and and_5 (and_5_out, RW, decoder_1_out4);
  and and_6 (and_6_out, RW, decoder_1_out5);
  and and_7 (and_7_out, RW, decoder_1_out6);
  and and_8 (and_8_out, RW, decoder_1_out7);
  and and_9 (and_9_out, RW, decoder_1_out8);
  and and_10 (and_10_out, RW, decoder_1_out9);
  and and_11 (and_11_out, RW, decoder_1_out10);
  and and_12 (and_12_out, RW, decoder_1_out11);
  and and_13 (and_13_out, RW, decoder_1_out12);
  and and_14 (and_14_out, RW, decoder_1_out13);
  and and_15 (and_15_out, RW, decoder_1_out14);
  and and_16 (and_16_out, RW, decoder_1_out15);
  and and_17 (and_17_out, RW, decoder_1_out16);
  and and_18 (and_18_out, RW, decoder_1_out17);
  and and_19 (and_19_out, RW, decoder_1_out18);
  and and_20 (and_20_out, RW, decoder_1_out19);
  and and_21 (and_21_out, RW, decoder_1_out20);
  and and_22 (and_22_out, RW, decoder_1_out21);
  and and_23 (and_23_out, RW, decoder_1_out22);
  and and_24 (and_24_out, RW, decoder_1_out23);
  and and_25 (and_25_out, RW, decoder_1_out24);
  and and_26 (and_26_out, RW, decoder_1_out25);
  and and_27 (and_27_out, RW, decoder_1_out26);
  and and_28 (and_28_out, RW, decoder_1_out27);
  and and_29 (and_29_out, RW, decoder_1_out28);
  and and_30 (and_30_out, RW, decoder_1_out29);
  and and_31 (and_31_out, RW, decoder_1_out30);
  and and_32 (and_32_out, RW, decoder_1_out31);
  Register #(.width(32)) u_R0 (.D(DI), .en(and_1_out), .Q(R0), .clk(clk), .clr(Rst));
  Register #(.width(32)) u_R1 (.D(DI), .en(and_2_out), .Q(R1), .clk(clk), .clr(Rst));
  Register #(.width(32)) u_R2 (.D(DI), .en(and_3_out), .Q(R2), .clk(clk), .clr(Rst));
  Register #(.width(32)) u_R3 (.D(DI), .en(and_4_out), .Q(R3), .clk(clk), .clr(Rst));
  Register #(.width(32)) u_R4 (.D(DI), .en(and_5_out), .Q(R4), .clk(clk), .clr(Rst));
  Register #(.width(32)) u_R5 (.D(DI), .en(and_6_out), .Q(R5), .clk(clk), .clr(Rst));
  Register #(.width(32)) u_R6 (.D(DI), .en(and_7_out), .Q(R6), .clk(clk), .clr(Rst));
  Register #(.width(32)) u_R7 (.D(DI), .en(and_8_out), .Q(R7), .clk(clk), .clr(Rst));
  Register #(.width(32)) u_R8 (.D(DI), .en(and_9_out), .Q(R8), .clk(clk), .clr(Rst));
  Register #(.width(32)) u_R9 (.D(DI), .en(and_10_out), .Q(R9), .clk(clk), .clr(Rst));
  Register #(.width(32)) u_R10 (.D(DI), .en(and_11_out), .Q(R10), .clk(clk), .clr(Rst));
  Register #(.width(32)) u_R11 (.D(DI), .en(and_12_out), .Q(R11), .clk(clk), .clr(Rst));
  Register #(.width(32)) u_R12 (.D(DI), .en(and_13_out), .Q(R12), .clk(clk), .clr(Rst));
  Register #(.width(32)) u_R13 (.D(DI), .en(and_14_out), .Q(R13), .clk(clk), .clr(Rst));
  Register #(.width(32)) u_R14 (.D(DI), .en(and_15_out), .Q(R14), .clk(clk), .clr(Rst));
  Register #(.width(32)) u_R15 (.D(DI), .en(and_16_out), .Q(R15), .clk(clk), .clr(Rst));
  Register #(.width(32)) u_R16 (.D(DI), .en(and_17_out), .Q(R16), .clk(clk), .clr(Rst));
  Register #(.width(32)) u_R17 (.D(DI), .en(and_18_out), .Q(R17), .clk(clk), .clr(Rst));
  Register #(.width(32)) u_R18 (.D(DI), .en(and_19_out), .Q(R18), .clk(clk), .clr(Rst));
  Register #(.width(32)) u_R19 (.D(DI), .en(and_20_out), .Q(R19), .clk(clk), .clr(Rst));
  Register #(.width(32)) u_R20 (.D(DI), .en(and_21_out), .Q(R20), .clk(clk), .clr(Rst));
  Register #(.width(32)) u_R21 (.D(DI), .en(and_22_out), .Q(R21), .clk(clk), .clr(Rst));
  Register #(.width(32)) u_R22 (.D(DI), .en(and_23_out), .Q(R22), .clk(clk), .clr(Rst));
  Register #(.width(32)) u_R23 (.D(DI), .en(and_24_out), .Q(R23), .clk(clk), .clr(Rst));
  Register #(.width(32)) u_R24 (.D(DI), .en(and_25_out), .Q(R24), .clk(clk), .clr(Rst));
  Register #(.width(32)) u_R25 (.D(DI), .en(and_26_out), .Q(R25), .clk(clk), .clr(Rst));
  Register #(.width(32)) u_R26 (.D(DI), .en(and_27_out), .Q(R26), .clk(clk), .clr(Rst));
  Register #(.width(32)) u_R27 (.D(DI), .en(and_28_out), .Q(R27), .clk(clk), .clr(Rst));
  Register #(.width(32)) u_R28 (.D(DI), .en(and_29_out), .Q(R28), .clk(clk), .clr(Rst));
  Register #(.width(32)) u_R29 (.D(DI), .en(and_30_out), .Q(R29), .clk(clk), .clr(Rst));
  Register #(.width(32)) u_R30 (.D(DI), .en(and_31_out), .Q(R30), .clk(clk), .clr(Rst));
  Register #(.width(32)) u_R31 (.D(DI), .en(and_32_out), .Q(R31), .clk(clk), .clr(Rst));
  Multiplexer #(.select(5), .width(32), .enable("false")) multiplexer_1 (
    .in0(R0), .in1(R1), .in2(R2), .in3(R3), .in4(R4), .in5(R5), .in6(R6), .in7(R7), .in8(R8), .in9(R9),
    .in10(R10), .in11(R11), .in12(R12), .in13(R13), .in14(R14), .in15(R15), .in16(R16), .in17(R17),
    .in18(R18), .in19(R19), .in20(R20), .in21(R21), .in22(R22), .in23(R23), .in24(R24), .in25(R25),
    .in26(R26), .in27(R27), .in28(R28), .in29(R29), .in30(R30), .in31(R31), .out(A), .sel(Sa));
  Multiplexer #(.select(5), .width(32), .enable("false")) multiplexer_2 (
    .in0(R0), .in1(R1), .in2(R2), .in3(R3), .in4(R4), .in5(R5), .in6(R6), .in7(R7), .in8(R8), .in9(R9),
    .in10(R10), .in11(R11), .in12(R12), .in13(R13), .in14(R14), .in15(R15), .in16(R16), .in17(R17),
    .in18(R18), .in19(R19), .in20(R20), .in21(R21), .in22(R22), .in23(R23), .in24(R24), .in25(R25),
    .in26(R26), .in27(R27), .in28(R28), .in29(R29), .in30(R30), .in31(R31), .out(B), .sel(Sb));
endmodule

module Instruction_Decoder (
  input  [31:0] inst,
  input  Wid,
  output [4:0] DA,
  output RW,
  output [4:0] Sa,
  output [4:0] Sb,
  output Jmp,
  output [25:0] k,
  output [3:0] Op
);

  wire _000, _0000, _00000, _0001, _001, _0010, _10, _0100, _0110, _1000, _1001, _1010, _1111, add, addi,
       \and , and_1_out, and_2_out, and_3_out, and_4_out, and_8_out, and_9_out, and_10_out, and_11_out,
       and_12_out, and_13_out, and_14_out, and_15_out, and_25_out, and_26_out, and_27_out, and_28_out,
       and_29_out, and_30_out, and_31_out, and_32_out, and_33_out, and_34_out, and_35_out, and_36_out,
       and_37_out, and_38_out, and_39_out, and_40_out, and_41_out, and_42_out, and_43_out, and_44_out,
       and_45_out, and_49_out, and_50_out, and_51_out, and_52_out, and_53_out, and_54_out, and_55_out,
       and_56_out, and_70_out, and_71_out, and_85_out, andi, beq, blez, bltz, bne, bqtz, div, divu, halt, j,
       jr, kbd, lw, mfhi, mflo, mult, mulu, nop, \nor , not_1_out, not_2_out, not_3_out, not_4_out,
       not_5_out, not_6_out, not_7_out, not_9_out, not_10_out, not_11_out, not_12_out, not_13_out,
       not_14_out, not_15_out, not_16_out, not_17_out, not_18_out, not_19_out, not_20_out, not_21_out,
       not_22_out, not_23_out, not_24_out, not_25_out, not_26_out, not_27_out, not_28_out, not_29_out, \or ,
       pop, push, R_Type_0, R_Type_1, R_Type_10, rnd, slt, slti, sltu, sub, sw, tty, \xor ;

  not not_1 (not_1_out, inst[4]);
  not not_2 (not_2_out, inst[5]);
  not not_3 (not_3_out, inst[4]);
  not not_4 (not_4_out, inst[31]);
  not not_5 (not_5_out, inst[30]);
  not not_6 (not_6_out, inst[31]);
  not not_7 (not_7_out, inst[30]);
  not not_8 (not_7_out, inst[29]);
  and and_1 (and_1_out, not_1_out, not_2_out);
  and and_2 (and_2_out, not_2_out, inst[4]);
  and and_3 (and_3_out, inst[4], inst[5]);
  and and_4 (and_4_out, inst[5], not_3_out);
  not not_9 (not_9_out, inst[2]);
  and and_5 (_001, not_4_out, not_5_out, inst[29]);
  and and_6 (_000, not_6_out, not_7_out, not_7_out);
  and and_7 (_10, inst[31], not_10_out);
  not not_10 (not_10_out, inst[30]);
  and and_8 (and_8_out, inst[3], not_9_out);
  not not_11 (not_11_out, inst[3]);
  not not_12 (not_12_out, inst[2]);
  not not_13 (not_13_out, inst[0]);
  not not_14 (not_14_out, inst[1]);
  and and_9 (and_9_out, not_11_out, not_12_out);
  and and_10 (and_10_out, not_11_out, inst[2]);
  and and_11 (and_11_out, inst[2], inst[3]);
  and and_12 (and_12_out, inst[1], inst[0]);
  and and_13 (and_13_out, inst[1], not_13_out);
  and and_14 (and_14_out, not_14_out, inst[0]);
  and and_15 (and_15_out, not_14_out, not_13_out);
  not not_15 (not_15_out, inst[0]);
  and and_16 (_0000, and_1_out, and_9_out);
  not not_16 (not_16_out, inst[1]);
  and and_17 (_0100, and_2_out, and_9_out);
  and and_18 (_0110, and_2_out, and_8_out);
  and and_19 (_00000, _0000, not_16_out);
  and and_20 (_1000, and_4_out, and_9_out);
  and and_21 (_1001, and_4_out, and_10_out);
  not not_17 (not_17_out, inst[26]);
  not not_18 (not_18_out, inst[27]);
  not not_19 (not_19_out, inst[28]);
  not not_20 (not_20_out, inst[29]);
  not not_21 (not_21_out, inst[30]);
  not not_22 (not_22_out, inst[31]);
  not not_23 (not_23_out, inst[28]);
  not not_24 (not_24_out, inst[27]);
  not not_25 (not_25_out, inst[26]);
  not not_26 (not_26_out, inst[28]);
  not not_27 (not_27_out, inst[27]);
  not not_28 (not_28_out, inst[26]);
  and and_22 (_0001, and_10_out, and_1_out);
  and and_23 (_0010, and_1_out, and_8_out);
  and and_24 (_1010, and_8_out, and_4_out);
  and and_25 (and_25_out, and_12_out, _1001);
  and and_26 (and_26_out, and_13_out, _1000);
  and and_27 (and_27_out, and_14_out, _1001);
  and and_28 (and_28_out, and_15_out, _1000);
  and and_29 (and_29_out, and_15_out, _1001);
  and and_30 (and_30_out, and_15_out, _1010);
  and and_31 (and_31_out, and_13_out, _1010);
  and and_32 (and_32_out, and_12_out, _1010);
  and and_33 (and_33_out, and_15_out, _0110);
  and and_34 (and_34_out, and_14_out, _0110);
  and and_35 (and_35_out, and_13_out, _0110);
  and and_36 (and_36_out, and_12_out, _0110);
  and and_37 (and_37_out, and_15_out, _0100);
  and and_38 (and_38_out, and_13_out, _0100);
  and and_39 (and_39_out, and_15_out, _0000);
  and and_40 (and_40_out, and_15_out, _0010);
  and and_41 (and_41_out, not_15_out, _00000);
  and and_42 (and_42_out, inst[0], _00000);
  and and_43 (and_43_out, inst[1], _1111);
  and and_44 (and_44_out, and_13_out, _0000);
  and and_45 (and_45_out, and_15_out, _0001);
  and and_46 (R_Type_0, not_17_out, not_18_out, not_19_out, not_20_out, not_21_out, not_22_out);
  and and_47 (R_Type_1, inst[26], inst[27], inst[28], inst[29], inst[30], inst[31]);
  and and_48 (R_Type_10, inst[31], inst[30], inst[29], not_23_out, not_24_out, not_25_out);
  and and_49 (and_49_out, not_26_out, not_27_out, not_28_out);
  and and_50 (and_50_out, inst[28], not_27_out, not_28_out);
  and and_51 (and_51_out, not_26_out, inst[27], not_28_out);
  and and_52 (and_52_out, not_26_out, inst[27], inst[26]);
  and and_53 (and_53_out, inst[28], not_27_out, inst[26]);
  and and_54 (and_54_out, inst[28], inst[27], not_28_out);
  and and_55 (and_55_out, inst[28], inst[27], inst[26]);
  and and_56 (and_56_out, not_26_out, not_27_out, inst[26]);
  not not_29 (not_29_out, inst[29]);
  and and_57 (_1111, and_3_out, and_11_out);
  and and_58 (\or , R_Type_0, and_27_out);
  and and_59 (add, R_Type_0, and_28_out);
  and and_60 (\and , R_Type_0, and_29_out);
  and and_61 (\xor , R_Type_0, and_30_out);
  and and_62 (slt, R_Type_0, and_31_out);
  and and_63 (sltu, R_Type_0, and_32_out);
  and and_64 (jr, R_Type_0, and_40_out);
  and and_65 (halt, R_Type_1, and_43_out);
  and and_66 (slti, and_51_out, _001);
  and and_67 (bne, and_53_out, _000);
  and and_68 (bqtz, and_55_out, _000);
  and and_69 (bltz, and_56_out, _000);
  and and_70 (and_70_out, not_29_out, not_26_out, inst[27], inst[26]);
  and and_71 (and_71_out, inst[29], not_26_out, inst[27], inst[26]);
  and and_72 (\nor , R_Type_0, and_25_out);
  and and_73 (sub, R_Type_0, and_26_out);
  and and_74 (mult, R_Type_0, and_33_out);
  and and_75 (mulu, R_Type_0, and_34_out);
  and and_76 (div, R_Type_0, and_35_out);
  and and_77 (divu, R_Type_0, and_36_out);
  and and_78 (mfhi, R_Type_0, and_37_out);
  and and_79 (mflo, R_Type_0, and_38_out);
  and and_80 (nop, R_Type_0, and_39_out);
  and and_81 (pop, R_Type_10, and_41_out);
  and and_82 (rnd, R_Type_1, and_44_out);
  and and_83 (kbd, R_Type_1, and_45_out);
  and and_84 (addi, and_49_out, _001);
  and and_85 (and_85_out, and_52_out, _001);
  and and_86 (j, and_51_out, _000);
  and and_87 (lw, and_70_out, _10);
  and and_88 (sw, and_71_out, _10);
  and and_89 (blez, and_54_out, _000);
  and and_90 (push, R_Type_10, and_42_out);
  and and_91 (tty, R_Type_1, and_42_out);
  and and_92 (andi, and_50_out, _001);
  and and_93 (beq, and_50_out, _000);
  or or_1 (RW, \nor , sub, \or , add, \and , \xor , slt, sltu, mult, mulu, div, divu, push);

  assign DA = inst[15:11];
  assign Sa = inst[25:21];
  assign Sb = inst[20:16];

  // Other names for the same wires on the sheet: Func_0 = inst[0]; Func_code[5:0] = inst[5:0]; Func_1 = inst[1];
  //   Func_2 = inst[2]; Func_3 = inst[3]; Func_4 = inst[4]; Func_5 = inst[5]; Rd[4:0] = inst[15:11];
  //   Op_code[5:0] = inst[31:26]; Rs[4:0] = inst[25:21]; Rt[4:0] = inst[20:16]

  // Notes on the sheet:
  //   Func-code
  //   x
  //   Rd
  //   Rt
  //   Rs
  //   Op-code
  //   00
  //   01
  //   11
  //   10
  //   001
  //   000
  //   10
  //   10
  //   Trabajo con el Func-Code
  //   00
  //   01
  //   11
  //   11
  //   10
  //   01
  //   00
  //   1000
  //   1010
  //   1001
  //   R Type 111111
  //   R Type 111000
  //   100
  //   010
  //   011
  //   101
  //   110
  //   111
  //   001
  //   R Type 000000
  //   000
  //   0011
  //   1011
  //   nor
  //   sub
  //   or
  //   add
  //   and
  //   xor
  //   slt
  //   sltu
  //   mult
  //   mulu
  //   div
  //   divu
  //   mfhi
  //   mflo
  //   nop
  //   jr
  //   pop
  //   halt
  //   rnd
  //   kbd
  //   push
  //   tty
  //   addi
  //   andi
  //   beq
  //   slti
  //   sltiu
  //   bne
  //   blez
  //   bqtz
  //   bltz
  //   j
  //   lw
  //   sw
endmodule
